# Fritzing sketch esp32_bme680_circuit (saved by Fritzing 0.9.3b)

parts:
  U3 = LuaNode32 / ESP32
  Part1 = Adafruit BME680

nets:
  3V3: U3.3V3, Part1.VIN
  GND: U3.GND, Part1.GND
  N1: U3.D21, Part1.SDI/SDA
  N2: U3.D22, Part1.SCK/SCL

custom parts:
  LuaNode32 / ESP32: ESP32 based LuaNode32
